# Fritzing sketch MF_A320_ELEC_BATT_OLED (saved by Fritzing 0.9.3b)

parts:
  Bauteil1 = Arduino Mega 2560 (Rev3)
  OLED_I2C1 = OLED 128x64 I2C Monochrome Display
  Bauteil2 = Adafruit TCA9548A
  OLED_I2C2 = OLED 128x64 I2C Monochrome Display

nets:
  N1: Bauteil1.D21/SCL, Bauteil2.INPUTSCL
  N2: Bauteil1.D20/SDA, Bauteil2.INPUTSDA
  GND: Bauteil1.GND, Bauteil2.GND
  VDD: Bauteil1.3V3, OLED_I2C1.VDD, Bauteil2.VCC, OLED_I2C2.VDD
  N3: OLED_I2C1.SDA, Bauteil2.0SDA
  N4: OLED_I2C1.SCK, Bauteil2.0SCL
  N5: Bauteil2.1SDA, OLED_I2C2.SDA
  N6: Bauteil2.1SCL, OLED_I2C2.SCK

custom parts:
  Adafruit TCA9548A: You just found the perfect I2C sensor, and you want to wire up two or three or more of them to your Arduino when you realize "Uh oh, this chip has a fixed I2C address, and from what I know about I2C, you cannot have two devices with the same address on the same SDA/SCL pins!" Are you out of luck? You would be, if you didn't have this ultra-cool TCA9548A 1-to-8 I2C multiplexer! Finally, a way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
